// Logisim project CONTROL UNIT.circ as structural Verilog
module PC (
  input  T0,
  input  T1,
  input  T3,
  input  T4,
  input  M201,
  input  M202,
  input  M203,
  input  M204,
  input  M205,
  input  M206,
  input  M207,
  input  M208,
  input  M209,
  input  M210,
  input  M211,
  input  M212,
  input  M213,
  input  M214,
  input  M215,
  input  M216,
  input  M217,
  input  M218,
  output PC_BUS,
  output PC_INC,
  output PC_LOAD
);

  wire and_1_out, and_2_out, and_3_out, and_4_out, and_5_out, and_6_out, and_7_out, and_8_out, and_9_out,
       and_10_out, and_11_out, and_12_out, and_13_out, and_14_out, and_15_out, and_16_out, and_17_out,
       and_18_out;

  and and_1 (and_1_out, M201, T4);
  and and_2 (and_2_out, M202, T3);
  and and_3 (and_3_out, M203, T3);
  and and_4 (and_4_out, M204, T4);
  and and_5 (and_5_out, M205, T3);
  and and_6 (and_6_out, M206, T3);
  and and_7 (and_7_out, M207, T4);
  and and_8 (and_8_out, M208, T3);
  and and_9 (and_9_out, M209, T3);
  and and_10 (and_10_out, M210, T4);
  and and_11 (and_11_out, M211, T3);
  and and_12 (and_12_out, M212, T3);
  and and_13 (and_13_out, M213, T4);
  and and_14 (and_14_out, M214, T3);
  and and_15 (and_15_out, M215, T3);
  and and_16 (and_16_out, M216, T4);
  and and_17 (and_17_out, M217, T3);
  and and_18 (and_18_out, M218, T3);
  or or_1 (PC_LOAD, and_1_out, and_2_out, and_3_out, and_4_out, and_5_out, and_6_out, and_7_out, and_8_out, and_9_out, and_10_out, and_11_out, and_12_out, and_13_out, and_14_out, and_15_out, and_16_out, and_17_out, and_18_out);

  assign PC_BUS = T0;
  assign PC_INC = T1;
endmodule
