// Logisim project CONTROL_UNITS.circ as structural Verilog: 1 circuit, main circuit CONTROL_UNIT
module CONTROL_UNIT (
  input  [23:0] IR,
  input  C,
  input  Z,
  input  CLK,
  output HLT,
  output AX_1,
  output BX_1,
  output CX_1,
  output DX_1,
  output EX_1,
  output AND,
  output OR,
  output XOR,
  output ADD,
  output ADC,
  output SUB,
  output SBB,
  output MUL,
  output DIV,
  output CMP,
  output LOAD,
  output AX_2,
  output BX_2,
  output CX_2,
  output DX_2,
  output EX_2,
  output DR_2,
  output IR_2,
  output MEM_STR,
  output MEM_BUS,
  output [2:0] MEM_MUX,
  output AX_INC,
  output AX_DEX,
  output AX_SHL,
  output AX_SHR,
  output AX_CIL,
  output AX_CIR,
  output AX_CML,
  output AX_CLR,
  output AX_LOAD,
  output AX_BUS,
  output BX_INC,
  output BX_DEX,
  output BX_SHL,
  output BX_SHR,
  output BX_CIL,
  output BX_CIR,
  output BX_CML,
  output BX_CLR,
  output BX_LOAD,
  output BX_BUS,
  output CX_INC,
  output CX_DEX,
  output CX_SHL,
  output CX_SHR,
  output CX_CIL,
  output CX_CIR,
  output CX_CML,
  output CX_CLR,
  output CX_LOAD,
  output CX_BUS,
  output DX_INC,
  output DX_DEX,
  output DX_SHL,
  output DX_SHR,
  output DX_CIL,
  output DX_CIR,
  output DX_CML,
  output DX_CLR,
  output DX_LOAD,
  output DX_BUS,
  output EX_INC,
  output EX_DEX,
  output EX_SHL,
  output EX_SHR,
  output EX_CIL,
  output EX_CIR,
  output EX_CML,
  output EX_CLR,
  output EX_LOAD,
  output EX_BUS,
  output PC_BUS,
  output PC_INC,
  output PC_LOAD,
  output IR_BUS,
  output IR_LOAD,
  output AR_LOAD,
  output AR_BUS,
  output DR_LOAD,
  output Z_LOAD,
  output Z_CLR,
  output Z_CML,
  output C_LOAD,
  output C_CLR,
  output C_CML
);

  wire counter_reset_1_counter_clr, e_signal_decoder_1__0, e_signal_decoder_1__1, e_signal_decoder_1__2,
       e_signal_decoder_1__3, e_signal_decoder_1__4, e_signal_decoder_1__5, e_signal_decoder_1__6,
       e_signal_decoder_1__7, e_signal_decoder_1__8, e_signal_decoder_1__9, e_signal_decoder_1__10,
       e_signal_decoder_1__11, e_signal_decoder_1__12, e_signal_decoder_1__13, e_signal_decoder_1__14,
       e_signal_decoder_1__15, e_signal_decoder_1__16, e_signal_decoder_1__17, e_signal_decoder_1__18,
       e_signal_decoder_1__19, e_signal_decoder_1__20, e_signal_decoder_1__21, e_signal_decoder_1__22,
       e_signal_decoder_1__23, e_signal_decoder_1__24, m_signal_decoder_1__0, m_signal_decoder_1__1,
       m_signal_decoder_1__2, m_signal_decoder_1__3, m_signal_decoder_1__4, m_signal_decoder_1__5,
       m_signal_decoder_1__6, m_signal_decoder_1__7, m_signal_decoder_1__8, m_signal_decoder_1__9,
       m_signal_decoder_1__10, m_signal_decoder_1__11, m_signal_decoder_1__12, m_signal_decoder_1__13,
       m_signal_decoder_1__14, m_signal_decoder_1__15, m_signal_decoder_1__16, m_signal_decoder_1__17,
       m_signal_decoder_1__18, m_signal_decoder_1__19, m_signal_decoder_1__20, m_signal_decoder_1__21,
       m_signal_decoder_1__22, m_signal_decoder_1__23, m_signal_decoder_1__24, m_signal_decoder_1__25,
       m_signal_decoder_1__26, m_signal_decoder_1__27, m_signal_decoder_1__28, m_signal_decoder_1__29,
       m_signal_decoder_1__30, m_signal_decoder_1__31, m_signal_decoder_1__32, m_signal_decoder_1__33,
       m_signal_decoder_1__34, m_signal_decoder_1__35, m_signal_decoder_1__36, m_signal_decoder_1__37,
       m_signal_decoder_1__38, m_signal_decoder_1__39, m_signal_decoder_1__40, m_signal_decoder_1__41,
       m_signal_decoder_1__42, m_signal_decoder_1__43, m_signal_decoder_1__44, m_signal_decoder_1__45,
       m_signal_decoder_1__46, m_signal_decoder_1__47, m_signal_decoder_1__48, m_signal_decoder_1__49,
       m_signal_decoder_1__50, m_signal_decoder_1__51, m_signal_decoder_1__52, m_signal_decoder_1__53,
       m_signal_decoder_1__54, m_signal_decoder_1__55, m_signal_decoder_1__56, m_signal_decoder_1__57,
       m_signal_decoder_1__58, m_signal_decoder_1__59, m_signal_decoder_1__60, m_signal_decoder_1__61,
       m_signal_decoder_1__62, m_signal_decoder_1__63, m_signal_decoder_1__64, m_signal_decoder_1__65,
       m_signal_decoder_1__66, m_signal_decoder_1__67, m_signal_decoder_1__68, m_signal_decoder_1__69,
       m_signal_decoder_1__70, m_signal_decoder_1__71, m_signal_decoder_1__72, m_signal_decoder_1__73,
       m_signal_decoder_1__74, m_signal_decoder_1__75, m_signal_decoder_1__76, m_signal_decoder_1__77,
       m_signal_decoder_1__78, m_signal_decoder_1__79, m_signal_decoder_1__80, m_signal_decoder_1__81,
       m_signal_decoder_1__82, m_signal_decoder_1__83, m_signal_decoder_1__84, m_signal_decoder_1__85,
       m_signal_decoder_1__86, m_signal_decoder_1__87, m_signal_decoder_1__88, m_signal_decoder_1__89,
       m_signal_decoder_1__90, m_signal_decoder_1__91, m_signal_decoder_1__92, m_signal_decoder_1__93,
       m_signal_decoder_1__94, m_signal_decoder_1__95, m_signal_decoder_1__96, m_signal_decoder_1__97,
       m_signal_decoder_1__98, m_signal_decoder_1__99, m_signal_decoder_1__100, m_signal_decoder_1__101,
       m_signal_decoder_1__102, m_signal_decoder_1__103, m_signal_decoder_1__104, m_signal_decoder_1__105,
       m_signal_decoder_1__106, m_signal_decoder_1__107, m_signal_decoder_1__108, m_signal_decoder_1__109,
       m_signal_decoder_1__110, m_signal_decoder_1__111, m_signal_decoder_1__112, m_signal_decoder_1__113,
       m_signal_decoder_1__114, m_signal_decoder_1__115, m_signal_decoder_1__116, m_signal_decoder_1__117,
       m_signal_decoder_1__118, m_signal_decoder_1__119, m_signal_decoder_1__120, m_signal_decoder_1__121,
       m_signal_decoder_1__122, m_signal_decoder_1__123, m_signal_decoder_1__124, m_signal_decoder_1__125,
       m_signal_decoder_1__126, m_signal_decoder_1__127, m_signal_decoder_1__128, m_signal_decoder_1__129,
       m_signal_decoder_1__130, m_signal_decoder_1__131, m_signal_decoder_1__132, m_signal_decoder_1__133,
       m_signal_decoder_1__134, m_signal_decoder_1__135, m_signal_decoder_1__136, m_signal_decoder_1__137,
       m_signal_decoder_1__138, m_signal_decoder_1__139, m_signal_decoder_1__140, m_signal_decoder_1__141,
       m_signal_decoder_1__142, m_signal_decoder_1__143, m_signal_decoder_1__144, m_signal_decoder_1__145,
       m_signal_decoder_1__146, m_signal_decoder_1__147, m_signal_decoder_1__148, m_signal_decoder_1__149,
       m_signal_decoder_1__150, m_signal_decoder_1__151, m_signal_decoder_1__152, m_signal_decoder_1__153,
       m_signal_decoder_1__154, m_signal_decoder_1__155, m_signal_decoder_1__156, m_signal_decoder_1__157,
       m_signal_decoder_1__158, m_signal_decoder_1__159, m_signal_decoder_1__160, m_signal_decoder_1__161,
       m_signal_decoder_1__162, m_signal_decoder_1__163, m_signal_decoder_1__164, m_signal_decoder_1__165,
       m_signal_decoder_1__166, m_signal_decoder_1__167, m_signal_decoder_1__168, m_signal_decoder_1__169,
       m_signal_decoder_1__170, m_signal_decoder_1__171, m_signal_decoder_1__172, m_signal_decoder_1__173,
       m_signal_decoder_1__174, m_signal_decoder_1__175, m_signal_decoder_1__176, m_signal_decoder_1__177,
       m_signal_decoder_1__178, m_signal_decoder_1__179, m_signal_decoder_1__180, m_signal_decoder_1__181,
       m_signal_decoder_1__182, m_signal_decoder_1__183, m_signal_decoder_1__184, m_signal_decoder_1__185,
       m_signal_decoder_1__186, m_signal_decoder_1__187, m_signal_decoder_1__188, m_signal_decoder_1__189,
       m_signal_decoder_1__190, m_signal_decoder_1__191, m_signal_decoder_1__192, m_signal_decoder_1__193,
       m_signal_decoder_1__194, m_signal_decoder_1__195, m_signal_decoder_1__196, m_signal_decoder_1__197,
       m_signal_decoder_1__198, m_signal_decoder_1__199, m_signal_decoder_1__200, m_signal_decoder_1__201,
       m_signal_decoder_1__202, m_signal_decoder_1__203, m_signal_decoder_1__204, m_signal_decoder_1__205,
       m_signal_decoder_1__206, m_signal_decoder_1__207, m_signal_decoder_1__208, m_signal_decoder_1__209,
       m_signal_decoder_1__210, m_signal_decoder_1__211, m_signal_decoder_1__212, m_signal_decoder_1__213,
       m_signal_decoder_1__214, m_signal_decoder_1__215, m_signal_decoder_1__216, m_signal_decoder_1__217,
       m_signal_decoder_1__218, m_signal_decoder_1__219, m_signal_decoder_1__220, m_signal_decoder_1__221,
       m_signal_decoder_1__222, m_signal_decoder_1__223, m_signal_decoder_1__224, m_signal_decoder_1__225,
       t_signal_producer_1__0, t_signal_producer_1__1, t_signal_producer_1__2, t_signal_producer_1__3,
       t_signal_producer_1__4, t_signal_producer_1__5;

  T_SIGNAL_PRODUCER t_signal_producer_1 (
    .CLK(CLK), .CLR(counter_reset_1_counter_clr), ._0(t_signal_producer_1__0), ._1(t_signal_producer_1__1),
    ._2(t_signal_producer_1__2), ._3(t_signal_producer_1__3), ._4(t_signal_producer_1__4),
    ._5(t_signal_producer_1__5));
  E_SIGNAL_DECODER e_signal_decoder_1 (
    .IR_4_0(IR[4:0]), ._0(e_signal_decoder_1__0), ._1(e_signal_decoder_1__1), ._2(e_signal_decoder_1__2),
    ._3(e_signal_decoder_1__3), ._4(e_signal_decoder_1__4), ._5(e_signal_decoder_1__5),
    ._6(e_signal_decoder_1__6), ._7(e_signal_decoder_1__7), ._8(e_signal_decoder_1__8),
    ._9(e_signal_decoder_1__9), ._10(e_signal_decoder_1__10), ._11(e_signal_decoder_1__11),
    ._12(e_signal_decoder_1__12), ._13(e_signal_decoder_1__13), ._14(e_signal_decoder_1__14),
    ._15(e_signal_decoder_1__15), ._16(e_signal_decoder_1__16), ._17(e_signal_decoder_1__17),
    ._18(e_signal_decoder_1__18), ._19(e_signal_decoder_1__19), ._20(e_signal_decoder_1__20),
    ._21(e_signal_decoder_1__21), ._22(e_signal_decoder_1__22), ._23(e_signal_decoder_1__23),
    ._24(e_signal_decoder_1__24));
  M_SIGNAL_DECODER m_signal_decoder_1 (
    .IR_23_16(IR[23:16]), ._0(m_signal_decoder_1__0), ._1(m_signal_decoder_1__1), ._2(m_signal_decoder_1__2),
    ._3(m_signal_decoder_1__3), ._4(m_signal_decoder_1__4), ._5(m_signal_decoder_1__5),
    ._6(m_signal_decoder_1__6), ._7(m_signal_decoder_1__7), ._8(m_signal_decoder_1__8),
    ._9(m_signal_decoder_1__9), ._10(m_signal_decoder_1__10), ._11(m_signal_decoder_1__11),
    ._12(m_signal_decoder_1__12), ._13(m_signal_decoder_1__13), ._14(m_signal_decoder_1__14),
    ._15(m_signal_decoder_1__15), ._16(m_signal_decoder_1__16), ._17(m_signal_decoder_1__17),
    ._18(m_signal_decoder_1__18), ._19(m_signal_decoder_1__19), ._20(m_signal_decoder_1__20),
    ._21(m_signal_decoder_1__21), ._22(m_signal_decoder_1__22), ._23(m_signal_decoder_1__23),
    ._24(m_signal_decoder_1__24), ._25(m_signal_decoder_1__25), ._26(m_signal_decoder_1__26),
    ._27(m_signal_decoder_1__27), ._28(m_signal_decoder_1__28), ._29(m_signal_decoder_1__29),
    ._30(m_signal_decoder_1__30), ._31(m_signal_decoder_1__31), ._32(m_signal_decoder_1__32),
    ._33(m_signal_decoder_1__33), ._34(m_signal_decoder_1__34), ._35(m_signal_decoder_1__35),
    ._36(m_signal_decoder_1__36), ._37(m_signal_decoder_1__37), ._38(m_signal_decoder_1__38),
    ._39(m_signal_decoder_1__39), ._40(m_signal_decoder_1__40), ._41(m_signal_decoder_1__41),
    ._42(m_signal_decoder_1__42), ._43(m_signal_decoder_1__43), ._44(m_signal_decoder_1__44),
    ._45(m_signal_decoder_1__45), ._46(m_signal_decoder_1__46), ._47(m_signal_decoder_1__47),
    ._48(m_signal_decoder_1__48), ._49(m_signal_decoder_1__49), ._50(m_signal_decoder_1__50),
    ._51(m_signal_decoder_1__51), ._52(m_signal_decoder_1__52), ._53(m_signal_decoder_1__53),
    ._54(m_signal_decoder_1__54), ._55(m_signal_decoder_1__55), ._56(m_signal_decoder_1__56),
    ._57(m_signal_decoder_1__57), ._58(m_signal_decoder_1__58), ._59(m_signal_decoder_1__59),
    ._60(m_signal_decoder_1__60), ._61(m_signal_decoder_1__61), ._62(m_signal_decoder_1__62),
    ._63(m_signal_decoder_1__63), ._64(m_signal_decoder_1__64), ._65(m_signal_decoder_1__65),
    ._66(m_signal_decoder_1__66), ._67(m_signal_decoder_1__67), ._68(m_signal_decoder_1__68),
    ._69(m_signal_decoder_1__69), ._70(m_signal_decoder_1__70), ._71(m_signal_decoder_1__71),
    ._72(m_signal_decoder_1__72), ._73(m_signal_decoder_1__73), ._74(m_signal_decoder_1__74),
    ._75(m_signal_decoder_1__75), ._76(m_signal_decoder_1__76), ._77(m_signal_decoder_1__77),
    ._78(m_signal_decoder_1__78), ._79(m_signal_decoder_1__79), ._80(m_signal_decoder_1__80),
    ._81(m_signal_decoder_1__81), ._82(m_signal_decoder_1__82), ._83(m_signal_decoder_1__83),
    ._84(m_signal_decoder_1__84), ._85(m_signal_decoder_1__85), ._86(m_signal_decoder_1__86),
    ._87(m_signal_decoder_1__87), ._88(m_signal_decoder_1__88), ._89(m_signal_decoder_1__89),
    ._90(m_signal_decoder_1__90), ._91(m_signal_decoder_1__91), ._92(m_signal_decoder_1__92),
    ._93(m_signal_decoder_1__93), ._94(m_signal_decoder_1__94), ._95(m_signal_decoder_1__95),
    ._96(m_signal_decoder_1__96), ._97(m_signal_decoder_1__97), ._98(m_signal_decoder_1__98),
    ._99(m_signal_decoder_1__99), ._100(m_signal_decoder_1__100), ._101(m_signal_decoder_1__101),
    ._102(m_signal_decoder_1__102), ._103(m_signal_decoder_1__103), ._104(m_signal_decoder_1__104),
    ._105(m_signal_decoder_1__105), ._106(m_signal_decoder_1__106), ._107(m_signal_decoder_1__107),
    ._108(m_signal_decoder_1__108), ._109(m_signal_decoder_1__109), ._110(m_signal_decoder_1__110),
    ._111(m_signal_decoder_1__111), ._112(m_signal_decoder_1__112), ._113(m_signal_decoder_1__113),
    ._114(m_signal_decoder_1__114), ._115(m_signal_decoder_1__115), ._116(m_signal_decoder_1__116),
    ._117(m_signal_decoder_1__117), ._118(m_signal_decoder_1__118), ._119(m_signal_decoder_1__119),
    ._120(m_signal_decoder_1__120), ._121(m_signal_decoder_1__121), ._122(m_signal_decoder_1__122),
    ._123(m_signal_decoder_1__123), ._124(m_signal_decoder_1__124), ._125(m_signal_decoder_1__125),
    ._126(m_signal_decoder_1__126), ._127(m_signal_decoder_1__127), ._128(m_signal_decoder_1__128),
    ._129(m_signal_decoder_1__129), ._130(m_signal_decoder_1__130), ._131(m_signal_decoder_1__131),
    ._132(m_signal_decoder_1__132), ._133(m_signal_decoder_1__133), ._134(m_signal_decoder_1__134),
    ._135(m_signal_decoder_1__135), ._136(m_signal_decoder_1__136), ._137(m_signal_decoder_1__137),
    ._138(m_signal_decoder_1__138), ._139(m_signal_decoder_1__139), ._140(m_signal_decoder_1__140),
    ._141(m_signal_decoder_1__141), ._142(m_signal_decoder_1__142), ._143(m_signal_decoder_1__143),
    ._144(m_signal_decoder_1__144), ._145(m_signal_decoder_1__145), ._146(m_signal_decoder_1__146),
    ._147(m_signal_decoder_1__147), ._148(m_signal_decoder_1__148), ._149(m_signal_decoder_1__149),
    ._150(m_signal_decoder_1__150), ._151(m_signal_decoder_1__151), ._152(m_signal_decoder_1__152),
    ._153(m_signal_decoder_1__153), ._154(m_signal_decoder_1__154), ._155(m_signal_decoder_1__155),
    ._156(m_signal_decoder_1__156), ._157(m_signal_decoder_1__157), ._158(m_signal_decoder_1__158),
    ._159(m_signal_decoder_1__159), ._160(m_signal_decoder_1__160), ._161(m_signal_decoder_1__161),
    ._162(m_signal_decoder_1__162), ._163(m_signal_decoder_1__163), ._164(m_signal_decoder_1__164),
    ._165(m_signal_decoder_1__165), ._166(m_signal_decoder_1__166), ._167(m_signal_decoder_1__167),
    ._168(m_signal_decoder_1__168), ._169(m_signal_decoder_1__169), ._170(m_signal_decoder_1__170),
    ._171(m_signal_decoder_1__171), ._172(m_signal_decoder_1__172), ._173(m_signal_decoder_1__173),
    ._174(m_signal_decoder_1__174), ._175(m_signal_decoder_1__175), ._176(m_signal_decoder_1__176),
    ._177(m_signal_decoder_1__177), ._178(m_signal_decoder_1__178), ._179(m_signal_decoder_1__179),
    ._180(m_signal_decoder_1__180), ._181(m_signal_decoder_1__181), ._182(m_signal_decoder_1__182),
    ._183(m_signal_decoder_1__183), ._184(m_signal_decoder_1__184), ._185(m_signal_decoder_1__185),
    ._186(m_signal_decoder_1__186), ._187(m_signal_decoder_1__187), ._188(m_signal_decoder_1__188),
    ._189(m_signal_decoder_1__189), ._190(m_signal_decoder_1__190), ._191(m_signal_decoder_1__191),
    ._192(m_signal_decoder_1__192), ._193(m_signal_decoder_1__193), ._194(m_signal_decoder_1__194),
    ._195(m_signal_decoder_1__195), ._196(m_signal_decoder_1__196), ._197(m_signal_decoder_1__197),
    ._198(m_signal_decoder_1__198), ._199(m_signal_decoder_1__199), ._200(m_signal_decoder_1__200),
    ._201(m_signal_decoder_1__201), ._202(m_signal_decoder_1__202), ._203(m_signal_decoder_1__203),
    ._204(m_signal_decoder_1__204), ._205(m_signal_decoder_1__205), ._206(m_signal_decoder_1__206),
    ._207(m_signal_decoder_1__207), ._208(m_signal_decoder_1__208), ._209(m_signal_decoder_1__209),
    ._210(m_signal_decoder_1__210), ._211(m_signal_decoder_1__211), ._212(m_signal_decoder_1__212),
    ._213(m_signal_decoder_1__213), ._214(m_signal_decoder_1__214), ._215(m_signal_decoder_1__215),
    ._216(m_signal_decoder_1__216), ._217(m_signal_decoder_1__217), ._218(m_signal_decoder_1__218),
    ._219(m_signal_decoder_1__219), ._220(m_signal_decoder_1__220), ._221(m_signal_decoder_1__221),
    ._222(m_signal_decoder_1__222), ._223(m_signal_decoder_1__223), ._224(m_signal_decoder_1__224),
    ._225(m_signal_decoder_1__225), ._226(HLT));
  COUNTER_RESET counter_reset_1 (
    .COUNTER_CLR(counter_reset_1_counter_clr), .T3(t_signal_producer_1__3), .T4(t_signal_producer_1__4),
    .T5(t_signal_producer_1__5), .M0(m_signal_decoder_1__0), .M1(m_signal_decoder_1__1),
    .M2(m_signal_decoder_1__2), .M3(m_signal_decoder_1__3), .M4(m_signal_decoder_1__4),
    .M5(m_signal_decoder_1__5), .M6(m_signal_decoder_1__6), .M7(m_signal_decoder_1__7),
    .M8(m_signal_decoder_1__8), .M9(m_signal_decoder_1__9), .M10(m_signal_decoder_1__10),
    .M11(m_signal_decoder_1__11), .M12(m_signal_decoder_1__12), .M13(m_signal_decoder_1__13),
    .M14(m_signal_decoder_1__14), .M15(m_signal_decoder_1__15), .M16(m_signal_decoder_1__16),
    .M17(m_signal_decoder_1__17), .M18(m_signal_decoder_1__18), .M19(m_signal_decoder_1__19),
    .M20(m_signal_decoder_1__20), .M21(m_signal_decoder_1__21), .M22(m_signal_decoder_1__22),
    .M23(m_signal_decoder_1__23), .M24(m_signal_decoder_1__24), .M25(m_signal_decoder_1__25),
    .M26(m_signal_decoder_1__26), .M27(m_signal_decoder_1__27), .M28(m_signal_decoder_1__28),
    .M29(m_signal_decoder_1__29), .M30(m_signal_decoder_1__30), .M31(m_signal_decoder_1__31),
    .M32(m_signal_decoder_1__32), .M33(m_signal_decoder_1__33), .M34(m_signal_decoder_1__34),
    .M35(m_signal_decoder_1__35), .M36(m_signal_decoder_1__36), .M37(m_signal_decoder_1__37),
    .M38(m_signal_decoder_1__38), .M39(m_signal_decoder_1__39), .M40(m_signal_decoder_1__40),
    .M41(m_signal_decoder_1__41), .M42(m_signal_decoder_1__42), .M43(m_signal_decoder_1__43),
    .M44(m_signal_decoder_1__44), .M45(m_signal_decoder_1__45), .M46(m_signal_decoder_1__46),
    .M47(m_signal_decoder_1__47), .M48(m_signal_decoder_1__48), .M49(m_signal_decoder_1__49),
    .M50(m_signal_decoder_1__50), .M51(m_signal_decoder_1__51), .M52(m_signal_decoder_1__52),
    .M53(m_signal_decoder_1__53), .M54(m_signal_decoder_1__54), .M55(m_signal_decoder_1__55),
    .M56(m_signal_decoder_1__56), .M57(m_signal_decoder_1__57), .M58(m_signal_decoder_1__58),
    .M59(m_signal_decoder_1__59), .M60(m_signal_decoder_1__60), .M61(m_signal_decoder_1__61),
    .M62(m_signal_decoder_1__62), .M63(m_signal_decoder_1__63), .M64(m_signal_decoder_1__64),
    .M65(m_signal_decoder_1__65), .M66(m_signal_decoder_1__66), .M67(m_signal_decoder_1__67),
    .M68(m_signal_decoder_1__68), .M69(m_signal_decoder_1__69), .M70(m_signal_decoder_1__70),
    .M71(m_signal_decoder_1__71), .M72(m_signal_decoder_1__72), .M73(m_signal_decoder_1__73),
    .M74(m_signal_decoder_1__74), .M75(m_signal_decoder_1__75), .M76(m_signal_decoder_1__76),
    .M77(m_signal_decoder_1__77), .M78(m_signal_decoder_1__78), .M79(m_signal_decoder_1__79),
    .M80(m_signal_decoder_1__80), .M81(m_signal_decoder_1__81), .M82(m_signal_decoder_1__82),
    .M83(m_signal_decoder_1__83), .M84(m_signal_decoder_1__84), .M85(m_signal_decoder_1__85),
    .M86(m_signal_decoder_1__86), .M87(m_signal_decoder_1__87), .M88(m_signal_decoder_1__88),
    .M89(m_signal_decoder_1__89), .M90(m_signal_decoder_1__90), .M91(m_signal_decoder_1__91),
    .M92(m_signal_decoder_1__92), .M93(m_signal_decoder_1__93), .M94(m_signal_decoder_1__94),
    .M95(m_signal_decoder_1__95), .M96(m_signal_decoder_1__96), .M97(m_signal_decoder_1__97),
    .M98(m_signal_decoder_1__98), .M99(m_signal_decoder_1__99), .M100(m_signal_decoder_1__100),
    .M101(m_signal_decoder_1__101), .M102(m_signal_decoder_1__102), .M103(m_signal_decoder_1__103),
    .M104(m_signal_decoder_1__104), .M105(m_signal_decoder_1__105), .M106(m_signal_decoder_1__106),
    .M107(m_signal_decoder_1__107), .M108(m_signal_decoder_1__108), .M109(m_signal_decoder_1__109),
    .M110(m_signal_decoder_1__110), .M111(m_signal_decoder_1__111), .M112(m_signal_decoder_1__112),
    .M113(m_signal_decoder_1__113), .M114(m_signal_decoder_1__114), .M115(m_signal_decoder_1__115),
    .M116(m_signal_decoder_1__116), .M117(m_signal_decoder_1__117), .M118(m_signal_decoder_1__118),
    .M119(m_signal_decoder_1__119), .M120(m_signal_decoder_1__120), .M121(m_signal_decoder_1__121),
    .M122(m_signal_decoder_1__122), .M123(m_signal_decoder_1__123), .M124(m_signal_decoder_1__124),
    .M125(m_signal_decoder_1__125), .M126(m_signal_decoder_1__126), .M127(m_signal_decoder_1__127),
    .M128(m_signal_decoder_1__128), .M129(m_signal_decoder_1__129), .M130(m_signal_decoder_1__130),
    .M131(m_signal_decoder_1__131), .M132(m_signal_decoder_1__132), .M133(m_signal_decoder_1__133),
    .M134(m_signal_decoder_1__134), .M135(m_signal_decoder_1__135), .M136(m_signal_decoder_1__136),
    .M137(m_signal_decoder_1__137), .M138(m_signal_decoder_1__138), .M139(m_signal_decoder_1__139),
    .M140(m_signal_decoder_1__140), .M141(m_signal_decoder_1__141), .M142(m_signal_decoder_1__142),
    .M143(m_signal_decoder_1__143), .M144(m_signal_decoder_1__144), .M145(m_signal_decoder_1__145),
    .M146(m_signal_decoder_1__146), .M147(m_signal_decoder_1__147), .M148(m_signal_decoder_1__148),
    .M149(m_signal_decoder_1__149), .M150(m_signal_decoder_1__150), .M151(m_signal_decoder_1__151),
    .M152(m_signal_decoder_1__152), .M153(m_signal_decoder_1__153), .M154(m_signal_decoder_1__154),
    .M155(m_signal_decoder_1__155), .M156(m_signal_decoder_1__156), .M157(m_signal_decoder_1__157),
    .M158(m_signal_decoder_1__158), .M159(m_signal_decoder_1__159), .M160(m_signal_decoder_1__160),
    .M161(m_signal_decoder_1__161), .M162(m_signal_decoder_1__162), .M163(m_signal_decoder_1__163),
    .M164(m_signal_decoder_1__164), .M165(m_signal_decoder_1__165), .M166(m_signal_decoder_1__166),
    .M167(m_signal_decoder_1__167), .M168(m_signal_decoder_1__168), .M169(m_signal_decoder_1__169),
    .M170(m_signal_decoder_1__170), .M171(m_signal_decoder_1__171), .M172(m_signal_decoder_1__172),
    .M173(m_signal_decoder_1__173), .M174(m_signal_decoder_1__174), .M175(m_signal_decoder_1__175),
    .M176(m_signal_decoder_1__176), .M177(m_signal_decoder_1__177), .M178(m_signal_decoder_1__178),
    .M179(m_signal_decoder_1__179), .M180(m_signal_decoder_1__180), .M181(m_signal_decoder_1__181),
    .M182(m_signal_decoder_1__182), .M183(m_signal_decoder_1__183), .M184(m_signal_decoder_1__184),
    .M185(m_signal_decoder_1__185), .M186(m_signal_decoder_1__186), .M187(m_signal_decoder_1__187),
    .M188(m_signal_decoder_1__188), .M189(m_signal_decoder_1__189), .M190(m_signal_decoder_1__190),
    .M191(m_signal_decoder_1__191), .M192(m_signal_decoder_1__192), .M193(m_signal_decoder_1__193),
    .M194(m_signal_decoder_1__194), .M195(m_signal_decoder_1__195), .M196(m_signal_decoder_1__196),
    .M197(m_signal_decoder_1__197), .M198(m_signal_decoder_1__198), .M199(m_signal_decoder_1__199),
    .M200(m_signal_decoder_1__200), .M201(m_signal_decoder_1__201), .M202(m_signal_decoder_1__202),
    .M203(m_signal_decoder_1__203), .M204(m_signal_decoder_1__204), .M205(m_signal_decoder_1__205),
    .M206(m_signal_decoder_1__206), .M207(m_signal_decoder_1__207), .M208(m_signal_decoder_1__208),
    .M209(m_signal_decoder_1__209), .M210(m_signal_decoder_1__210), .M211(m_signal_decoder_1__211),
    .M212(m_signal_decoder_1__212), .M213(m_signal_decoder_1__213), .M214(m_signal_decoder_1__214),
    .M215(m_signal_decoder_1__215), .M216(m_signal_decoder_1__216), .M217(m_signal_decoder_1__217),
    .M218(m_signal_decoder_1__218), .M219(m_signal_decoder_1__219), .M220(m_signal_decoder_1__220),
    .M221(m_signal_decoder_1__221), .M222(m_signal_decoder_1__222), .M223(m_signal_decoder_1__223),
    .M224(m_signal_decoder_1__224), .M225(m_signal_decoder_1__225));
  SPECIAL_PURPOSE special_purpose_1 (
    .C(C), .Z(Z), .T0(t_signal_producer_1__0), .T1(t_signal_producer_1__1), .T2(t_signal_producer_1__2),
    .T3(t_signal_producer_1__3), .T4(t_signal_producer_1__4), .T5(t_signal_producer_1__5),
    .M0(m_signal_decoder_1__0), .M1(m_signal_decoder_1__1), .M2(m_signal_decoder_1__2),
    .M3(m_signal_decoder_1__3), .M4(m_signal_decoder_1__4), .M5(m_signal_decoder_1__5),
    .M6(m_signal_decoder_1__6), .M7(m_signal_decoder_1__7), .M8(m_signal_decoder_1__8),
    .M9(m_signal_decoder_1__9), .M15(m_signal_decoder_1__15), .M17(m_signal_decoder_1__17),
    .M18(m_signal_decoder_1__18), .M19(m_signal_decoder_1__19), .M20(m_signal_decoder_1__20),
    .M21(m_signal_decoder_1__21), .M22(m_signal_decoder_1__22), .M23(m_signal_decoder_1__23),
    .M24(m_signal_decoder_1__24), .M25(m_signal_decoder_1__25), .M26(m_signal_decoder_1__26),
    .M32(m_signal_decoder_1__32), .M34(m_signal_decoder_1__34), .M35(m_signal_decoder_1__35),
    .M36(m_signal_decoder_1__36), .M37(m_signal_decoder_1__37), .M38(m_signal_decoder_1__38),
    .M39(m_signal_decoder_1__39), .M40(m_signal_decoder_1__40), .M41(m_signal_decoder_1__41),
    .M42(m_signal_decoder_1__42), .M43(m_signal_decoder_1__43), .M49(m_signal_decoder_1__49),
    .M51(m_signal_decoder_1__51), .M52(m_signal_decoder_1__52), .M53(m_signal_decoder_1__53),
    .M54(m_signal_decoder_1__54), .M55(m_signal_decoder_1__55), .M56(m_signal_decoder_1__56),
    .M57(m_signal_decoder_1__57), .M58(m_signal_decoder_1__58), .M59(m_signal_decoder_1__59),
    .M60(m_signal_decoder_1__60), .M66(m_signal_decoder_1__66), .M68(m_signal_decoder_1__68),
    .M69(m_signal_decoder_1__69), .M70(m_signal_decoder_1__70), .M71(m_signal_decoder_1__71),
    .M72(m_signal_decoder_1__72), .M73(m_signal_decoder_1__73), .M74(m_signal_decoder_1__74),
    .M75(m_signal_decoder_1__75), .M76(m_signal_decoder_1__76), .M77(m_signal_decoder_1__77),
    .M83(m_signal_decoder_1__83), .M85(m_signal_decoder_1__85), .M86(m_signal_decoder_1__86),
    .M87(m_signal_decoder_1__87), .M88(m_signal_decoder_1__88), .M89(m_signal_decoder_1__89),
    .M90(m_signal_decoder_1__90), .M91(m_signal_decoder_1__91), .M92(m_signal_decoder_1__92),
    .M93(m_signal_decoder_1__93), .M94(m_signal_decoder_1__94), .M100(m_signal_decoder_1__100),
    .M102(m_signal_decoder_1__102), .M103(m_signal_decoder_1__103), .M104(m_signal_decoder_1__104),
    .M105(m_signal_decoder_1__105), .M106(m_signal_decoder_1__106), .M107(m_signal_decoder_1__107),
    .M108(m_signal_decoder_1__108), .M109(m_signal_decoder_1__109), .M110(m_signal_decoder_1__110),
    .M111(m_signal_decoder_1__111), .M117(m_signal_decoder_1__117), .M119(m_signal_decoder_1__119),
    .M120(m_signal_decoder_1__120), .M121(m_signal_decoder_1__121), .M122(m_signal_decoder_1__122),
    .M123(m_signal_decoder_1__123), .M124(m_signal_decoder_1__124), .M125(m_signal_decoder_1__125),
    .M126(m_signal_decoder_1__126), .M127(m_signal_decoder_1__127), .M128(m_signal_decoder_1__128),
    .M134(m_signal_decoder_1__134), .M136(m_signal_decoder_1__136), .M137(m_signal_decoder_1__137),
    .M138(m_signal_decoder_1__138), .M139(m_signal_decoder_1__139), .M140(m_signal_decoder_1__140),
    .M141(m_signal_decoder_1__141), .M142(m_signal_decoder_1__142), .M143(m_signal_decoder_1__143),
    .M144(m_signal_decoder_1__144), .M145(m_signal_decoder_1__145), .M151(m_signal_decoder_1__151),
    .M153(m_signal_decoder_1__153), .M154(m_signal_decoder_1__154), .M155(m_signal_decoder_1__155),
    .M156(m_signal_decoder_1__156), .M157(m_signal_decoder_1__157), .M158(m_signal_decoder_1__158),
    .M159(m_signal_decoder_1__159), .M160(m_signal_decoder_1__160), .M161(m_signal_decoder_1__161),
    .M162(m_signal_decoder_1__162), .M168(m_signal_decoder_1__168), .M170(m_signal_decoder_1__170),
    .M171(m_signal_decoder_1__171), .M172(m_signal_decoder_1__172), .M173(m_signal_decoder_1__173),
    .M174(m_signal_decoder_1__174), .M175(m_signal_decoder_1__175), .M176(m_signal_decoder_1__176),
    .M177(m_signal_decoder_1__177), .M178(m_signal_decoder_1__178), .M179(m_signal_decoder_1__179),
    .M180(m_signal_decoder_1__180), .M181(m_signal_decoder_1__181), .M182(m_signal_decoder_1__182),
    .M183(m_signal_decoder_1__183), .M184(m_signal_decoder_1__184), .M190(m_signal_decoder_1__190),
    .M191(m_signal_decoder_1__191), .M192(m_signal_decoder_1__192), .M193(m_signal_decoder_1__193),
    .M194(m_signal_decoder_1__194), .M196(m_signal_decoder_1__196), .M197(m_signal_decoder_1__197),
    .M198(m_signal_decoder_1__198), .M199(m_signal_decoder_1__199), .M200(m_signal_decoder_1__200),
    .M201(m_signal_decoder_1__201), .M202(m_signal_decoder_1__202), .M203(m_signal_decoder_1__203),
    .M204(m_signal_decoder_1__204), .M205(m_signal_decoder_1__205), .M206(m_signal_decoder_1__206),
    .M207(m_signal_decoder_1__207), .M208(m_signal_decoder_1__208), .M209(m_signal_decoder_1__209),
    .M210(m_signal_decoder_1__210), .M211(m_signal_decoder_1__211), .M212(m_signal_decoder_1__212),
    .M213(m_signal_decoder_1__213), .PC_BUS(PC_BUS), .PC_INC(PC_INC), .PC_LOAD(PC_LOAD), .IR_BUS(IR_BUS),
    .IR_LOAD(IR_LOAD), .AR_LOAD(AR_LOAD), .AR_BUS(AR_BUS), .DR_LOAD(DR_LOAD));
  MEMORY memory_1 (
    .T1(t_signal_producer_1__1), .T3(t_signal_producer_1__3), .T4(t_signal_producer_1__4),
    .E0(e_signal_decoder_1__0), .E1(e_signal_decoder_1__1), .E2(e_signal_decoder_1__2),
    .E3(e_signal_decoder_1__3), .E4(e_signal_decoder_1__4), .E5(e_signal_decoder_1__5),
    .E6(e_signal_decoder_1__6), .E7(e_signal_decoder_1__7), .E8(e_signal_decoder_1__8),
    .E9(e_signal_decoder_1__9), .E10(e_signal_decoder_1__10), .E11(e_signal_decoder_1__11),
    .E12(e_signal_decoder_1__12), .E13(e_signal_decoder_1__13), .E14(e_signal_decoder_1__14),
    .E15(e_signal_decoder_1__15), .E16(e_signal_decoder_1__16), .E17(e_signal_decoder_1__17),
    .E18(e_signal_decoder_1__18), .E19(e_signal_decoder_1__19), .E20(e_signal_decoder_1__20),
    .E21(e_signal_decoder_1__21), .E22(e_signal_decoder_1__22), .E23(e_signal_decoder_1__23),
    .E24(e_signal_decoder_1__24), .M0(m_signal_decoder_1__0), .M1(m_signal_decoder_1__1),
    .M2(m_signal_decoder_1__2), .M3(m_signal_decoder_1__3), .M4(m_signal_decoder_1__4),
    .M5(m_signal_decoder_1__5), .M6(m_signal_decoder_1__6), .M7(m_signal_decoder_1__7),
    .M8(m_signal_decoder_1__8), .M9(m_signal_decoder_1__9), .M15(m_signal_decoder_1__15),
    .M17(m_signal_decoder_1__17), .M18(m_signal_decoder_1__18), .M19(m_signal_decoder_1__19),
    .M20(m_signal_decoder_1__20), .M21(m_signal_decoder_1__21), .M22(m_signal_decoder_1__22),
    .M23(m_signal_decoder_1__23), .M24(m_signal_decoder_1__24), .M25(m_signal_decoder_1__25),
    .M26(m_signal_decoder_1__26), .M32(m_signal_decoder_1__32), .M34(m_signal_decoder_1__34),
    .M35(m_signal_decoder_1__35), .M36(m_signal_decoder_1__36), .M37(m_signal_decoder_1__37),
    .M38(m_signal_decoder_1__38), .M39(m_signal_decoder_1__39), .M40(m_signal_decoder_1__40),
    .M41(m_signal_decoder_1__41), .M42(m_signal_decoder_1__42), .M43(m_signal_decoder_1__43),
    .M49(m_signal_decoder_1__49), .M51(m_signal_decoder_1__51), .M52(m_signal_decoder_1__52),
    .M53(m_signal_decoder_1__53), .M54(m_signal_decoder_1__54), .M55(m_signal_decoder_1__55),
    .M56(m_signal_decoder_1__56), .M57(m_signal_decoder_1__57), .M58(m_signal_decoder_1__58),
    .M59(m_signal_decoder_1__59), .M60(m_signal_decoder_1__60), .M66(m_signal_decoder_1__66),
    .M68(m_signal_decoder_1__68), .M69(m_signal_decoder_1__69), .M70(m_signal_decoder_1__70),
    .M71(m_signal_decoder_1__71), .M72(m_signal_decoder_1__72), .M73(m_signal_decoder_1__73),
    .M74(m_signal_decoder_1__74), .M75(m_signal_decoder_1__75), .M76(m_signal_decoder_1__76),
    .M77(m_signal_decoder_1__77), .M83(m_signal_decoder_1__83), .M85(m_signal_decoder_1__85),
    .M86(m_signal_decoder_1__86), .M87(m_signal_decoder_1__87), .M88(m_signal_decoder_1__88),
    .M89(m_signal_decoder_1__89), .M90(m_signal_decoder_1__90), .M91(m_signal_decoder_1__91),
    .M92(m_signal_decoder_1__92), .M93(m_signal_decoder_1__93), .M94(m_signal_decoder_1__94),
    .M100(m_signal_decoder_1__100), .M102(m_signal_decoder_1__102), .M103(m_signal_decoder_1__103),
    .M104(m_signal_decoder_1__104), .M105(m_signal_decoder_1__105), .M106(m_signal_decoder_1__106),
    .M107(m_signal_decoder_1__107), .M108(m_signal_decoder_1__108), .M109(m_signal_decoder_1__109),
    .M110(m_signal_decoder_1__110), .M111(m_signal_decoder_1__111), .M117(m_signal_decoder_1__117),
    .M119(m_signal_decoder_1__119), .M120(m_signal_decoder_1__120), .M121(m_signal_decoder_1__121),
    .M122(m_signal_decoder_1__122), .M123(m_signal_decoder_1__123), .M124(m_signal_decoder_1__124),
    .M125(m_signal_decoder_1__125), .M126(m_signal_decoder_1__126), .M127(m_signal_decoder_1__127),
    .M128(m_signal_decoder_1__128), .M134(m_signal_decoder_1__134), .M136(m_signal_decoder_1__136),
    .M137(m_signal_decoder_1__137), .M138(m_signal_decoder_1__138), .M139(m_signal_decoder_1__139),
    .M140(m_signal_decoder_1__140), .M141(m_signal_decoder_1__141), .M142(m_signal_decoder_1__142),
    .M143(m_signal_decoder_1__143), .M144(m_signal_decoder_1__144), .M145(m_signal_decoder_1__145),
    .M151(m_signal_decoder_1__151), .M153(m_signal_decoder_1__153), .M154(m_signal_decoder_1__154),
    .M155(m_signal_decoder_1__155), .M156(m_signal_decoder_1__156), .M157(m_signal_decoder_1__157),
    .M158(m_signal_decoder_1__158), .M159(m_signal_decoder_1__159), .M160(m_signal_decoder_1__160),
    .M161(m_signal_decoder_1__161), .M162(m_signal_decoder_1__162), .M168(m_signal_decoder_1__168),
    .M170(m_signal_decoder_1__170), .M171(m_signal_decoder_1__171), .M172(m_signal_decoder_1__172),
    .M173(m_signal_decoder_1__173), .M174(m_signal_decoder_1__174), .M175(m_signal_decoder_1__175),
    .M176(m_signal_decoder_1__176), .M177(m_signal_decoder_1__177), .M178(m_signal_decoder_1__178),
    .M179(m_signal_decoder_1__179), .M180(m_signal_decoder_1__180), .M181(m_signal_decoder_1__181),
    .M182(m_signal_decoder_1__182), .M183(m_signal_decoder_1__183), .M184(m_signal_decoder_1__184),
    .M185(m_signal_decoder_1__185), .M186(m_signal_decoder_1__186), .M187(m_signal_decoder_1__187),
    .M188(m_signal_decoder_1__188), .M189(m_signal_decoder_1__189), .M196(m_signal_decoder_1__196),
    .M199(m_signal_decoder_1__199), .M202(m_signal_decoder_1__202), .M205(m_signal_decoder_1__205),
    .M208(m_signal_decoder_1__208), .M211(m_signal_decoder_1__211), .STR(MEM_STR), .BUS(MEM_BUS),
    .MUX(MEM_MUX));
  FLAGS flags_1 (
    .T3(t_signal_producer_1__3), .T4(t_signal_producer_1__4), .T5(t_signal_producer_1__5),
    .M0(m_signal_decoder_1__0), .M1(m_signal_decoder_1__1), .M2(m_signal_decoder_1__2),
    .M3(m_signal_decoder_1__3), .M4(m_signal_decoder_1__4), .M5(m_signal_decoder_1__5),
    .M6(m_signal_decoder_1__6), .M7(m_signal_decoder_1__7), .M8(m_signal_decoder_1__8),
    .M9(m_signal_decoder_1__9), .M10(m_signal_decoder_1__10), .M11(m_signal_decoder_1__11),
    .M12(m_signal_decoder_1__12), .M13(m_signal_decoder_1__13), .M14(m_signal_decoder_1__14),
    .M15(m_signal_decoder_1__15), .M16(m_signal_decoder_1__16), .M17(m_signal_decoder_1__17),
    .M18(m_signal_decoder_1__18), .M19(m_signal_decoder_1__19), .M20(m_signal_decoder_1__20),
    .M21(m_signal_decoder_1__21), .M22(m_signal_decoder_1__22), .M23(m_signal_decoder_1__23),
    .M24(m_signal_decoder_1__24), .M25(m_signal_decoder_1__25), .M26(m_signal_decoder_1__26),
    .M27(m_signal_decoder_1__27), .M28(m_signal_decoder_1__28), .M29(m_signal_decoder_1__29),
    .M30(m_signal_decoder_1__30), .M31(m_signal_decoder_1__31), .M32(m_signal_decoder_1__32),
    .M33(m_signal_decoder_1__33), .M34(m_signal_decoder_1__34), .M35(m_signal_decoder_1__35),
    .M36(m_signal_decoder_1__36), .M37(m_signal_decoder_1__37), .M38(m_signal_decoder_1__38),
    .M39(m_signal_decoder_1__39), .M40(m_signal_decoder_1__40), .M41(m_signal_decoder_1__41),
    .M42(m_signal_decoder_1__42), .M43(m_signal_decoder_1__43), .M44(m_signal_decoder_1__44),
    .M45(m_signal_decoder_1__45), .M46(m_signal_decoder_1__46), .M47(m_signal_decoder_1__47),
    .M48(m_signal_decoder_1__48), .M49(m_signal_decoder_1__49), .M50(m_signal_decoder_1__50),
    .M51(m_signal_decoder_1__51), .M52(m_signal_decoder_1__52), .M53(m_signal_decoder_1__53),
    .M54(m_signal_decoder_1__54), .M55(m_signal_decoder_1__55), .M56(m_signal_decoder_1__56),
    .M57(m_signal_decoder_1__57), .M58(m_signal_decoder_1__58), .M59(m_signal_decoder_1__59),
    .M60(m_signal_decoder_1__60), .M61(m_signal_decoder_1__61), .M62(m_signal_decoder_1__62),
    .M63(m_signal_decoder_1__63), .M64(m_signal_decoder_1__64), .M65(m_signal_decoder_1__65),
    .M66(m_signal_decoder_1__66), .M67(m_signal_decoder_1__67), .M68(m_signal_decoder_1__68),
    .M69(m_signal_decoder_1__69), .M70(m_signal_decoder_1__70), .M71(m_signal_decoder_1__71),
    .M72(m_signal_decoder_1__72), .M73(m_signal_decoder_1__73), .M74(m_signal_decoder_1__74),
    .M75(m_signal_decoder_1__75), .M76(m_signal_decoder_1__76), .M77(m_signal_decoder_1__77),
    .M78(m_signal_decoder_1__78), .M79(m_signal_decoder_1__79), .M80(m_signal_decoder_1__80),
    .M81(m_signal_decoder_1__81), .M82(m_signal_decoder_1__82), .M83(m_signal_decoder_1__83),
    .M84(m_signal_decoder_1__84), .M85(m_signal_decoder_1__85), .M86(m_signal_decoder_1__86),
    .M87(m_signal_decoder_1__87), .M88(m_signal_decoder_1__88), .M89(m_signal_decoder_1__89),
    .M90(m_signal_decoder_1__90), .M91(m_signal_decoder_1__91), .M92(m_signal_decoder_1__92),
    .M93(m_signal_decoder_1__93), .M94(m_signal_decoder_1__94), .M95(m_signal_decoder_1__95),
    .M96(m_signal_decoder_1__96), .M97(m_signal_decoder_1__97), .M98(m_signal_decoder_1__98),
    .M99(m_signal_decoder_1__99), .M100(m_signal_decoder_1__100), .M101(m_signal_decoder_1__101),
    .M102(m_signal_decoder_1__102), .M103(m_signal_decoder_1__103), .M104(m_signal_decoder_1__104),
    .M105(m_signal_decoder_1__105), .M106(m_signal_decoder_1__106), .M107(m_signal_decoder_1__107),
    .M108(m_signal_decoder_1__108), .M109(m_signal_decoder_1__109), .M110(m_signal_decoder_1__110),
    .M111(m_signal_decoder_1__111), .M112(m_signal_decoder_1__112), .M113(m_signal_decoder_1__113),
    .M114(m_signal_decoder_1__114), .M115(m_signal_decoder_1__115), .M116(m_signal_decoder_1__116),
    .M117(m_signal_decoder_1__117), .M118(m_signal_decoder_1__118), .M119(m_signal_decoder_1__119),
    .M120(m_signal_decoder_1__120), .M121(m_signal_decoder_1__121), .M122(m_signal_decoder_1__122),
    .M123(m_signal_decoder_1__123), .M124(m_signal_decoder_1__124), .M125(m_signal_decoder_1__125),
    .M126(m_signal_decoder_1__126), .M127(m_signal_decoder_1__127), .M128(m_signal_decoder_1__128),
    .M129(m_signal_decoder_1__129), .M130(m_signal_decoder_1__130), .M131(m_signal_decoder_1__131),
    .M132(m_signal_decoder_1__132), .M133(m_signal_decoder_1__133), .M134(m_signal_decoder_1__134),
    .M135(m_signal_decoder_1__135), .M136(m_signal_decoder_1__136), .M137(m_signal_decoder_1__137),
    .M138(m_signal_decoder_1__138), .M139(m_signal_decoder_1__139), .M140(m_signal_decoder_1__140),
    .M141(m_signal_decoder_1__141), .M142(m_signal_decoder_1__142), .M143(m_signal_decoder_1__143),
    .M144(m_signal_decoder_1__144), .M145(m_signal_decoder_1__145), .M146(m_signal_decoder_1__146),
    .M147(m_signal_decoder_1__147), .M148(m_signal_decoder_1__148), .M149(m_signal_decoder_1__149),
    .M150(m_signal_decoder_1__150), .M151(m_signal_decoder_1__151), .M152(m_signal_decoder_1__152),
    .M153(m_signal_decoder_1__153), .M154(m_signal_decoder_1__154), .M155(m_signal_decoder_1__155),
    .M156(m_signal_decoder_1__156), .M157(m_signal_decoder_1__157), .M158(m_signal_decoder_1__158),
    .M159(m_signal_decoder_1__159), .M160(m_signal_decoder_1__160), .M161(m_signal_decoder_1__161),
    .M162(m_signal_decoder_1__162), .M163(m_signal_decoder_1__163), .M164(m_signal_decoder_1__164),
    .M165(m_signal_decoder_1__165), .M166(m_signal_decoder_1__166), .M167(m_signal_decoder_1__167),
    .M168(m_signal_decoder_1__168), .M169(m_signal_decoder_1__169), .M222(m_signal_decoder_1__222),
    .M223(m_signal_decoder_1__223), .M224(m_signal_decoder_1__224), .M225(m_signal_decoder_1__225),
    .Z_LOAD(Z_LOAD), .Z_CLR(Z_CLR), .Z_CML(Z_CML), .C_LOAD(C_LOAD), .C_CLR(C_CLR), .C_CML(C_CML));
  GENERAL_PURPOSE general_purpose_1 (
    .E0(e_signal_decoder_1__0), .E1(e_signal_decoder_1__1), .E2(e_signal_decoder_1__2),
    .E3(e_signal_decoder_1__3), .E4(e_signal_decoder_1__4), .E5(e_signal_decoder_1__5),
    .E6(e_signal_decoder_1__6), .E7(e_signal_decoder_1__7), .E8(e_signal_decoder_1__8),
    .E9(e_signal_decoder_1__9), .E10(e_signal_decoder_1__10), .E11(e_signal_decoder_1__11),
    .E12(e_signal_decoder_1__12), .E13(e_signal_decoder_1__13), .E14(e_signal_decoder_1__14),
    .E15(e_signal_decoder_1__15), .E16(e_signal_decoder_1__16), .E17(e_signal_decoder_1__17),
    .E18(e_signal_decoder_1__18), .E19(e_signal_decoder_1__19), .E20(e_signal_decoder_1__20),
    .E21(e_signal_decoder_1__21), .E22(e_signal_decoder_1__22), .E23(e_signal_decoder_1__23),
    .E24(e_signal_decoder_1__24), .T3(t_signal_producer_1__3), .T4(t_signal_producer_1__4),
    .T5(t_signal_producer_1__5), .C(C), .Z(Z), .M0(m_signal_decoder_1__0), .M1(m_signal_decoder_1__1),
    .M2(m_signal_decoder_1__2), .M3(m_signal_decoder_1__3), .M4(m_signal_decoder_1__4),
    .M5(m_signal_decoder_1__5), .M6(m_signal_decoder_1__6), .M7(m_signal_decoder_1__7),
    .M8(m_signal_decoder_1__8), .M9(m_signal_decoder_1__9), .M10(m_signal_decoder_1__10),
    .M11(m_signal_decoder_1__11), .M12(m_signal_decoder_1__12), .M13(m_signal_decoder_1__13),
    .M14(m_signal_decoder_1__14), .M15(m_signal_decoder_1__15), .M16(m_signal_decoder_1__16),
    .M17(m_signal_decoder_1__17), .M18(m_signal_decoder_1__18), .M19(m_signal_decoder_1__19),
    .M20(m_signal_decoder_1__20), .M21(m_signal_decoder_1__21), .M22(m_signal_decoder_1__22),
    .M23(m_signal_decoder_1__23), .M24(m_signal_decoder_1__24), .M25(m_signal_decoder_1__25),
    .M26(m_signal_decoder_1__26), .M27(m_signal_decoder_1__27), .M28(m_signal_decoder_1__28),
    .M29(m_signal_decoder_1__29), .M30(m_signal_decoder_1__30), .M31(m_signal_decoder_1__31),
    .M32(m_signal_decoder_1__32), .M33(m_signal_decoder_1__33), .M34(m_signal_decoder_1__34),
    .M35(m_signal_decoder_1__35), .M36(m_signal_decoder_1__36), .M37(m_signal_decoder_1__37),
    .M38(m_signal_decoder_1__38), .M39(m_signal_decoder_1__39), .M40(m_signal_decoder_1__40),
    .M41(m_signal_decoder_1__41), .M42(m_signal_decoder_1__42), .M43(m_signal_decoder_1__43),
    .M44(m_signal_decoder_1__44), .M45(m_signal_decoder_1__45), .M46(m_signal_decoder_1__46),
    .M47(m_signal_decoder_1__47), .M48(m_signal_decoder_1__48), .M49(m_signal_decoder_1__49),
    .M50(m_signal_decoder_1__50), .M51(m_signal_decoder_1__51), .M52(m_signal_decoder_1__52),
    .M53(m_signal_decoder_1__53), .M54(m_signal_decoder_1__54), .M55(m_signal_decoder_1__55),
    .M56(m_signal_decoder_1__56), .M57(m_signal_decoder_1__57), .M58(m_signal_decoder_1__58),
    .M59(m_signal_decoder_1__59), .M60(m_signal_decoder_1__60), .M61(m_signal_decoder_1__61),
    .M62(m_signal_decoder_1__62), .M63(m_signal_decoder_1__63), .M64(m_signal_decoder_1__64),
    .M65(m_signal_decoder_1__65), .M66(m_signal_decoder_1__66), .M67(m_signal_decoder_1__67),
    .M68(m_signal_decoder_1__68), .M69(m_signal_decoder_1__69), .M70(m_signal_decoder_1__70),
    .M71(m_signal_decoder_1__71), .M72(m_signal_decoder_1__72), .M73(m_signal_decoder_1__73),
    .M74(m_signal_decoder_1__74), .M75(m_signal_decoder_1__75), .M76(m_signal_decoder_1__76),
    .M77(m_signal_decoder_1__77), .M78(m_signal_decoder_1__78), .M79(m_signal_decoder_1__79),
    .M80(m_signal_decoder_1__80), .M81(m_signal_decoder_1__81), .M82(m_signal_decoder_1__82),
    .M83(m_signal_decoder_1__83), .M84(m_signal_decoder_1__84), .M85(m_signal_decoder_1__85),
    .M86(m_signal_decoder_1__86), .M87(m_signal_decoder_1__87), .M88(m_signal_decoder_1__88),
    .M89(m_signal_decoder_1__89), .M90(m_signal_decoder_1__90), .M91(m_signal_decoder_1__91),
    .M92(m_signal_decoder_1__92), .M93(m_signal_decoder_1__93), .M94(m_signal_decoder_1__94),
    .M95(m_signal_decoder_1__95), .M96(m_signal_decoder_1__96), .M97(m_signal_decoder_1__97),
    .M98(m_signal_decoder_1__98), .M99(m_signal_decoder_1__99), .M100(m_signal_decoder_1__100),
    .M101(m_signal_decoder_1__101), .M102(m_signal_decoder_1__102), .M103(m_signal_decoder_1__103),
    .M104(m_signal_decoder_1__104), .M105(m_signal_decoder_1__105), .M106(m_signal_decoder_1__106),
    .M107(m_signal_decoder_1__107), .M108(m_signal_decoder_1__108), .M109(m_signal_decoder_1__109),
    .M110(m_signal_decoder_1__110), .M111(m_signal_decoder_1__111), .M112(m_signal_decoder_1__112),
    .M113(m_signal_decoder_1__113), .M114(m_signal_decoder_1__114), .M115(m_signal_decoder_1__115),
    .M116(m_signal_decoder_1__116), .M117(m_signal_decoder_1__117), .M118(m_signal_decoder_1__118),
    .M119(m_signal_decoder_1__119), .M120(m_signal_decoder_1__120), .M121(m_signal_decoder_1__121),
    .M122(m_signal_decoder_1__122), .M123(m_signal_decoder_1__123), .M124(m_signal_decoder_1__124),
    .M125(m_signal_decoder_1__125), .M126(m_signal_decoder_1__126), .M127(m_signal_decoder_1__127),
    .M128(m_signal_decoder_1__128), .M129(m_signal_decoder_1__129), .M130(m_signal_decoder_1__130),
    .M131(m_signal_decoder_1__131), .M132(m_signal_decoder_1__132), .M133(m_signal_decoder_1__133),
    .M134(m_signal_decoder_1__134), .M135(m_signal_decoder_1__135), .M136(m_signal_decoder_1__136),
    .M137(m_signal_decoder_1__137), .M138(m_signal_decoder_1__138), .M139(m_signal_decoder_1__139),
    .M140(m_signal_decoder_1__140), .M141(m_signal_decoder_1__141), .M142(m_signal_decoder_1__142),
    .M143(m_signal_decoder_1__143), .M144(m_signal_decoder_1__144), .M145(m_signal_decoder_1__145),
    .M146(m_signal_decoder_1__146), .M147(m_signal_decoder_1__147), .M148(m_signal_decoder_1__148),
    .M149(m_signal_decoder_1__149), .M150(m_signal_decoder_1__150), .M151(m_signal_decoder_1__151),
    .M152(m_signal_decoder_1__152), .M170(m_signal_decoder_1__170), .M171(m_signal_decoder_1__171),
    .M172(m_signal_decoder_1__172), .M173(m_signal_decoder_1__173), .M174(m_signal_decoder_1__174),
    .M175(m_signal_decoder_1__175), .M176(m_signal_decoder_1__176), .M177(m_signal_decoder_1__177),
    .M178(m_signal_decoder_1__178), .M179(m_signal_decoder_1__179), .M180(m_signal_decoder_1__180),
    .M181(m_signal_decoder_1__181), .M182(m_signal_decoder_1__182), .M183(m_signal_decoder_1__183),
    .M184(m_signal_decoder_1__184), .M185(m_signal_decoder_1__185), .M186(m_signal_decoder_1__186),
    .M187(m_signal_decoder_1__187), .M188(m_signal_decoder_1__188), .M189(m_signal_decoder_1__189),
    .M190(m_signal_decoder_1__190), .M191(m_signal_decoder_1__191), .M192(m_signal_decoder_1__192),
    .M193(m_signal_decoder_1__193), .M194(m_signal_decoder_1__194), .M195(m_signal_decoder_1__195),
    .M198(m_signal_decoder_1__198), .M201(m_signal_decoder_1__201), .M204(m_signal_decoder_1__204),
    .M207(m_signal_decoder_1__207), .M210(m_signal_decoder_1__210), .M213(m_signal_decoder_1__213),
    .M214(m_signal_decoder_1__214), .M215(m_signal_decoder_1__215), .M216(m_signal_decoder_1__216),
    .M217(m_signal_decoder_1__217), .M218(m_signal_decoder_1__218), .M219(m_signal_decoder_1__219),
    .M220(m_signal_decoder_1__220), .M221(m_signal_decoder_1__221), .AX_INC(AX_INC), .AX_DEX(AX_DEX),
    .AX_SHL(AX_SHL), .AX_SHR(AX_SHR), .AX_CIL(AX_CIL), .AX_CIR(AX_CIR), .AX_CML(AX_CML), .AX_CLR(AX_CLR),
    .AX_LOAD(AX_LOAD), .AX_BUS(AX_BUS), .BX_INC(BX_INC), .BX_DEX(BX_DEX), .BX_SHL(BX_SHL), .BX_SHR(BX_SHR),
    .BX_CIL(BX_CIL), .BX_CIR(BX_CIR), .BX_CML(BX_CML), .BX_CLR(BX_CLR), .BX_LOAD(BX_LOAD), .BX_BUS(BX_BUS),
    .CX_INC(CX_INC), .CX_DEX(CX_DEX), .CX_SHL(CX_SHL), .CX_SHR(CX_SHR), .CX_CIL(CX_CIL), .CX_CIR(CX_CIR),
    .CX_CML(CX_CML), .CX_CLR(CX_CLR), .CX_LOAD(CX_LOAD), .CX_BUS(CX_BUS), .DX_INC(DX_INC), .DX_DEX(DX_DEX),
    .DX_SHL(DX_SHL), .DX_SHR(DX_SHR), .DX_CIL(DX_CIL), .DX_CIR(DX_CIR), .DX_CML(DX_CML), .DX_CLR(DX_CLR),
    .DX_LOAD(DX_LOAD), .DX_BUS(DX_BUS), .EX_INC(EX_INC), .EX_DEX(EX_DEX), .EX_SHL(EX_SHL), .EX_SHR(EX_SHR),
    .EX_CIL(EX_CIL), .EX_CIR(EX_CIR), .EX_CML(EX_CML), .EX_CLR(EX_CLR), .EX_LOAD(EX_LOAD), .EX_BUS(EX_BUS));
  ALU alu_1 (
    .T3(t_signal_producer_1__3), .T4(t_signal_producer_1__4), .T5(t_signal_producer_1__5),
    .E0(e_signal_decoder_1__0), .E1(e_signal_decoder_1__1), .E2(e_signal_decoder_1__2),
    .E3(e_signal_decoder_1__3), .E4(e_signal_decoder_1__4), .E5(e_signal_decoder_1__5),
    .E6(e_signal_decoder_1__6), .E7(e_signal_decoder_1__7), .E8(e_signal_decoder_1__8),
    .E9(e_signal_decoder_1__9), .E10(e_signal_decoder_1__10), .E11(e_signal_decoder_1__11),
    .E12(e_signal_decoder_1__12), .E13(e_signal_decoder_1__13), .E14(e_signal_decoder_1__14),
    .E15(e_signal_decoder_1__15), .E16(e_signal_decoder_1__16), .E17(e_signal_decoder_1__17),
    .E18(e_signal_decoder_1__18), .E19(e_signal_decoder_1__19), .E20(e_signal_decoder_1__20),
    .E21(e_signal_decoder_1__21), .E22(e_signal_decoder_1__22), .E23(e_signal_decoder_1__23),
    .E24(e_signal_decoder_1__24), .M0(m_signal_decoder_1__0), .M1(m_signal_decoder_1__1),
    .M2(m_signal_decoder_1__2), .M3(m_signal_decoder_1__3), .M4(m_signal_decoder_1__4),
    .M5(m_signal_decoder_1__5), .M6(m_signal_decoder_1__6), .M7(m_signal_decoder_1__7),
    .M8(m_signal_decoder_1__8), .M9(m_signal_decoder_1__9), .M10(m_signal_decoder_1__10),
    .M11(m_signal_decoder_1__11), .M12(m_signal_decoder_1__12), .M13(m_signal_decoder_1__13),
    .M14(m_signal_decoder_1__14), .M15(m_signal_decoder_1__15), .M16(m_signal_decoder_1__16),
    .M17(m_signal_decoder_1__17), .M18(m_signal_decoder_1__18), .M19(m_signal_decoder_1__19),
    .M20(m_signal_decoder_1__20), .M21(m_signal_decoder_1__21), .M22(m_signal_decoder_1__22),
    .M23(m_signal_decoder_1__23), .M24(m_signal_decoder_1__24), .M25(m_signal_decoder_1__25),
    .M26(m_signal_decoder_1__26), .M27(m_signal_decoder_1__27), .M28(m_signal_decoder_1__28),
    .M29(m_signal_decoder_1__29), .M30(m_signal_decoder_1__30), .M31(m_signal_decoder_1__31),
    .M32(m_signal_decoder_1__32), .M33(m_signal_decoder_1__33), .M34(m_signal_decoder_1__34),
    .M35(m_signal_decoder_1__35), .M36(m_signal_decoder_1__36), .M37(m_signal_decoder_1__37),
    .M38(m_signal_decoder_1__38), .M39(m_signal_decoder_1__39), .M40(m_signal_decoder_1__40),
    .M41(m_signal_decoder_1__41), .M42(m_signal_decoder_1__42), .M43(m_signal_decoder_1__43),
    .M44(m_signal_decoder_1__44), .M45(m_signal_decoder_1__45), .M46(m_signal_decoder_1__46),
    .M47(m_signal_decoder_1__47), .M48(m_signal_decoder_1__48), .M49(m_signal_decoder_1__49),
    .M50(m_signal_decoder_1__50), .M51(m_signal_decoder_1__51), .M52(m_signal_decoder_1__52),
    .M53(m_signal_decoder_1__53), .M54(m_signal_decoder_1__54), .M55(m_signal_decoder_1__55),
    .M56(m_signal_decoder_1__56), .M57(m_signal_decoder_1__57), .M58(m_signal_decoder_1__58),
    .M59(m_signal_decoder_1__59), .M60(m_signal_decoder_1__60), .M61(m_signal_decoder_1__61),
    .M62(m_signal_decoder_1__62), .M63(m_signal_decoder_1__63), .M64(m_signal_decoder_1__64),
    .M65(m_signal_decoder_1__65), .M66(m_signal_decoder_1__66), .M67(m_signal_decoder_1__67),
    .M68(m_signal_decoder_1__68), .M69(m_signal_decoder_1__69), .M70(m_signal_decoder_1__70),
    .M71(m_signal_decoder_1__71), .M72(m_signal_decoder_1__72), .M73(m_signal_decoder_1__73),
    .M74(m_signal_decoder_1__74), .M75(m_signal_decoder_1__75), .M76(m_signal_decoder_1__76),
    .M77(m_signal_decoder_1__77), .M78(m_signal_decoder_1__78), .M79(m_signal_decoder_1__79),
    .M80(m_signal_decoder_1__80), .M81(m_signal_decoder_1__81), .M82(m_signal_decoder_1__82),
    .M83(m_signal_decoder_1__83), .M84(m_signal_decoder_1__84), .M85(m_signal_decoder_1__85),
    .M86(m_signal_decoder_1__86), .M87(m_signal_decoder_1__87), .M88(m_signal_decoder_1__88),
    .M89(m_signal_decoder_1__89), .M90(m_signal_decoder_1__90), .M91(m_signal_decoder_1__91),
    .M92(m_signal_decoder_1__92), .M93(m_signal_decoder_1__93), .M94(m_signal_decoder_1__94),
    .M95(m_signal_decoder_1__95), .M96(m_signal_decoder_1__96), .M97(m_signal_decoder_1__97),
    .M98(m_signal_decoder_1__98), .M99(m_signal_decoder_1__99), .M100(m_signal_decoder_1__100),
    .M101(m_signal_decoder_1__101), .M102(m_signal_decoder_1__102), .M103(m_signal_decoder_1__103),
    .M104(m_signal_decoder_1__104), .M105(m_signal_decoder_1__105), .M106(m_signal_decoder_1__106),
    .M107(m_signal_decoder_1__107), .M108(m_signal_decoder_1__108), .M109(m_signal_decoder_1__109),
    .M110(m_signal_decoder_1__110), .M111(m_signal_decoder_1__111), .M112(m_signal_decoder_1__112),
    .M113(m_signal_decoder_1__113), .M114(m_signal_decoder_1__114), .M115(m_signal_decoder_1__115),
    .M116(m_signal_decoder_1__116), .M117(m_signal_decoder_1__117), .M118(m_signal_decoder_1__118),
    .M119(m_signal_decoder_1__119), .M120(m_signal_decoder_1__120), .M121(m_signal_decoder_1__121),
    .M122(m_signal_decoder_1__122), .M123(m_signal_decoder_1__123), .M124(m_signal_decoder_1__124),
    .M125(m_signal_decoder_1__125), .M126(m_signal_decoder_1__126), .M127(m_signal_decoder_1__127),
    .M128(m_signal_decoder_1__128), .M129(m_signal_decoder_1__129), .M130(m_signal_decoder_1__130),
    .M131(m_signal_decoder_1__131), .M132(m_signal_decoder_1__132), .M133(m_signal_decoder_1__133),
    .M134(m_signal_decoder_1__134), .M135(m_signal_decoder_1__135), .M136(m_signal_decoder_1__136),
    .M137(m_signal_decoder_1__137), .M138(m_signal_decoder_1__138), .M139(m_signal_decoder_1__139),
    .M140(m_signal_decoder_1__140), .M141(m_signal_decoder_1__141), .M142(m_signal_decoder_1__142),
    .M143(m_signal_decoder_1__143), .M144(m_signal_decoder_1__144), .M145(m_signal_decoder_1__145),
    .M146(m_signal_decoder_1__146), .M147(m_signal_decoder_1__147), .M148(m_signal_decoder_1__148),
    .M149(m_signal_decoder_1__149), .M150(m_signal_decoder_1__150), .M151(m_signal_decoder_1__151),
    .M152(m_signal_decoder_1__152), .M153(m_signal_decoder_1__153), .M154(m_signal_decoder_1__154),
    .M155(m_signal_decoder_1__155), .M156(m_signal_decoder_1__156), .M157(m_signal_decoder_1__157),
    .M158(m_signal_decoder_1__158), .M159(m_signal_decoder_1__159), .M160(m_signal_decoder_1__160),
    .M161(m_signal_decoder_1__161), .M162(m_signal_decoder_1__162), .M163(m_signal_decoder_1__163),
    .M164(m_signal_decoder_1__164), .M165(m_signal_decoder_1__165), .M166(m_signal_decoder_1__166),
    .M167(m_signal_decoder_1__167), .M168(m_signal_decoder_1__168), .M169(m_signal_decoder_1__169),
    .M170(m_signal_decoder_1__170), .M171(m_signal_decoder_1__171), .M172(m_signal_decoder_1__172),
    .M173(m_signal_decoder_1__173), .M174(m_signal_decoder_1__174), .M175(m_signal_decoder_1__175),
    .M176(m_signal_decoder_1__176), .M177(m_signal_decoder_1__177), .M178(m_signal_decoder_1__178),
    .M179(m_signal_decoder_1__179), .M190(m_signal_decoder_1__190), .M191(m_signal_decoder_1__191),
    .M192(m_signal_decoder_1__192), .M193(m_signal_decoder_1__193), .M194(m_signal_decoder_1__194),
    .M195(m_signal_decoder_1__195), .AX_1(AX_1), .BX_1(BX_1), .CX_1(CX_1), .DX_1(DX_1), .EX_1(EX_1),
    .AND(AND), .OR(OR), .XOR(XOR), .ADD(ADD), .ADC(ADC), .SUB(SUB), .SBB(SBB), .MUL(MUL), .DIV(DIV),
    .CMP(CMP), .LOAD(LOAD), .AX_2(AX_2), .BX_2(BX_2), .CX_2(CX_2), .DX_2(DX_2), .EX_2(EX_2), .DR_2(DR_2),
    .IR_2(IR_2));
endmodule
