// Logisim project Microprocessor.circ as structural Verilog: 2 circuits, main circuit main
module main (
);

  wire alu_1_cout, alu_1_zero, and_1_out, clock_1_out, control_unit_1_p1, control_unit_1_p2,
       control_unit_1_p3, control_unit_1_p4, control_unit_1_p5, control_unit_1_p6, control_unit_1_p7,
       control_unit_1_p31, control_unit_1_p32, control_unit_1_p43, control_unit_1_p53, control_unit_1_p63,
       control_unit_1_p73, control_unit_1_p83, control_unit_1_p84, control_unit_1_p85, control_unit_1_p86,
       control_unit_1_p87, control_unit_1_p88, control_unit_1_p89, control_unit_1_p90, control_unit_1_p91,
       control_unit_1_p92, control_unit_1_p93, control_unit_1_p94, control_unit_1_p95, control_unit_1_p96,
       control_unit_1_p97;
  wire [2:0] control_unit_1_p33;
  wire [4:0] control_unit_1_p8;
  wire [6:0] control_unit_1_p24;
  wire [7:0] instruction_register_1_output_2;
  wire [8:0] control_unit_1_p41, control_unit_1_p51, control_unit_1_p61, control_unit_1_p71,
       control_unit_1_p81;
  wire [10:0] control_unit_1_p23;
  wire [15:0] alu_1_ax_4, alu_1_bx_4, alu_1_cx_4, alu_1_dx_4, alu_1_ex_4, general_purpose_1_output,
       general_purpose_2_output, general_purpose_3_output, general_purpose_4_output,
       general_purpose_5_output, instruction_register_1_output, multiplexer_1_out, special_purpose_1_output,
       special_purpose_2_output, special_purpose_3_output;
  wire [23:0] controlled_buffer_1_out, ram_1_data;

  Clock clock_1 (.out(clock_1_out));
  // CONTROL_UNIT control_unit_1: pin names not known; wires that end beside it: control_unit_1_p1, control_unit_1_p2, control_unit_1_p3, control_unit_1_p4, control_unit_1_p5, control_unit_1_p6, control_unit_1_p7, control_unit_1_p8[0], control_unit_1_p8[1], control_unit_1_p8[2], control_unit_1_p8[3], control_unit_1_p8[4], control_unit_1_p23[10], control_unit_1_p23[9], control_unit_1_p23[8], control_unit_1_p23[7], control_unit_1_p23[6], control_unit_1_p23[5], control_unit_1_p23[4], control_unit_1_p23[3], control_unit_1_p23[2], control_unit_1_p23[1], control_unit_1_p23[0], control_unit_1_p24[0], control_unit_1_p24[1], control_unit_1_p24[2], control_unit_1_p24[3], control_unit_1_p24[4], control_unit_1_p24[5], control_unit_1_p24[6], control_unit_1_p31, control_unit_1_p32, control_unit_1_p33, control_unit_1_p41[8], control_unit_1_p41[6], control_unit_1_p41[5], control_unit_1_p41[4], control_unit_1_p41[3], control_unit_1_p41[2], control_unit_1_p41[1], control_unit_1_p41[0], control_unit_1_p41[7], control_unit_1_p43, control_unit_1_p51[8], control_unit_1_p51[6], control_unit_1_p51[5], control_unit_1_p51[4], control_unit_1_p51[3], control_unit_1_p51[2], control_unit_1_p51[1], control_unit_1_p51[0], control_unit_1_p51[7], control_unit_1_p53, control_unit_1_p61[8], control_unit_1_p61[6], control_unit_1_p61[5], control_unit_1_p61[4], control_unit_1_p61[3], control_unit_1_p61[2], control_unit_1_p61[1], control_unit_1_p61[0], control_unit_1_p61[7], control_unit_1_p63, control_unit_1_p71[8], control_unit_1_p71[6], control_unit_1_p71[5], control_unit_1_p71[4], control_unit_1_p71[3], control_unit_1_p71[2], control_unit_1_p71[1], control_unit_1_p71[0], control_unit_1_p71[7], control_unit_1_p73, control_unit_1_p81[8], control_unit_1_p81[6], control_unit_1_p81[5], control_unit_1_p81[4], control_unit_1_p81[3], control_unit_1_p81[2], control_unit_1_p81[1], control_unit_1_p81[0], control_unit_1_p81[7], control_unit_1_p83, control_unit_1_p84, control_unit_1_p85, control_unit_1_p86, control_unit_1_p87, control_unit_1_p88, control_unit_1_p89, control_unit_1_p90, control_unit_1_p91, control_unit_1_p92, control_unit_1_p93, control_unit_1_p94, control_unit_1_p95, control_unit_1_p96, control_unit_1_p97
  and and_1 (and_1_out, ~control_unit_1_p3, clock_1_out);  // AND_Gate
  FLAG flag_1 (
    .INPUT(alu_1_zero), .CLK(and_1_out), .LOAD(control_unit_1_p92), .CLR(control_unit_1_p93),
    .CML(control_unit_1_p94), .out_6(control_unit_1_p7));
  FLAG flag_2 (
    .INPUT(alu_1_cout), .CLK(and_1_out), .LOAD(control_unit_1_p95), .CLR(control_unit_1_p96),
    .CML(control_unit_1_p97), .out_6(control_unit_1_p6));
  ALU alu_1 (
    .Cin(control_unit_1_p6), .AX_2(control_unit_1_p8[0]), .BX_2(control_unit_1_p8[1]),
    .CX_2(control_unit_1_p8[2]), .DX_2(control_unit_1_p8[3]), .EX_2(control_unit_1_p8[4]), .DR_2(1'b0),
    .IR_2(1'b0), .AX_3(control_unit_1_p24[0]), .BX_3(control_unit_1_p24[1]), .CX_3(control_unit_1_p24[2]),
    .DX_3(control_unit_1_p24[3]), .EX_3(control_unit_1_p24[4]), .DR_3(control_unit_1_p24[5]),
    .IR_3(control_unit_1_p24[6]), .AX(general_purpose_1_output), .BX(general_purpose_2_output),
    .CX(general_purpose_3_output), .DX(general_purpose_4_output), .EX(general_purpose_5_output),
    .DR(special_purpose_3_output), .IR(instruction_register_1_output), .AND(control_unit_1_p23[10]),
    .OR(control_unit_1_p23[9]), .XOR(control_unit_1_p23[8]), .ADD(control_unit_1_p23[7]),
    .ADC(control_unit_1_p23[6]), .SUB(control_unit_1_p23[5]), .SBB(control_unit_1_p23[4]),
    .MUL(control_unit_1_p23[3]), .DIV(control_unit_1_p23[2]), .CMP(control_unit_1_p23[1]),
    .LOAD(control_unit_1_p23[0]), .AX_4(alu_1_ax_4), .BX_4(alu_1_bx_4), .CX_4(alu_1_cx_4), .DX_4(alu_1_dx_4),
    .EX_4(alu_1_ex_4), .Zero(alu_1_zero), .Cout(alu_1_cout));
  GENERAL_PURPOSE general_purpose_1 (
    .INPUT(alu_1_ax_4), .INC(control_unit_1_p41[8]), .LD(control_unit_1_p41[7]), .DEC(control_unit_1_p41[6]),
    .SHL(control_unit_1_p41[5]), .SHR(control_unit_1_p41[4]), .CIL(control_unit_1_p41[3]),
    .CIR(control_unit_1_p41[2]), .CML(control_unit_1_p41[1]), .CLR(control_unit_1_p41[0]), .CLK(and_1_out),
    .OUTPUT(general_purpose_1_output));
  GENERAL_PURPOSE general_purpose_2 (
    .INPUT(alu_1_bx_4), .INC(control_unit_1_p51[8]), .LD(control_unit_1_p51[7]), .DEC(control_unit_1_p51[6]),
    .SHL(control_unit_1_p51[5]), .SHR(control_unit_1_p51[4]), .CIL(control_unit_1_p51[3]),
    .CIR(control_unit_1_p51[2]), .CML(control_unit_1_p51[1]), .CLR(control_unit_1_p51[0]), .CLK(and_1_out),
    .OUTPUT(general_purpose_2_output));
  GENERAL_PURPOSE general_purpose_3 (
    .INPUT(alu_1_cx_4), .INC(control_unit_1_p61[8]), .LD(control_unit_1_p61[7]), .DEC(control_unit_1_p61[6]),
    .SHL(control_unit_1_p61[5]), .SHR(control_unit_1_p61[4]), .CIL(control_unit_1_p61[3]),
    .CIR(control_unit_1_p61[2]), .CML(control_unit_1_p61[1]), .CLR(control_unit_1_p61[0]), .CLK(and_1_out),
    .OUTPUT(general_purpose_3_output));
  GENERAL_PURPOSE general_purpose_4 (
    .INPUT(alu_1_dx_4), .INC(control_unit_1_p71[8]), .LD(control_unit_1_p71[7]), .DEC(control_unit_1_p71[6]),
    .SHL(control_unit_1_p71[5]), .SHR(control_unit_1_p71[4]), .CIL(control_unit_1_p71[3]),
    .CIR(control_unit_1_p71[2]), .CML(control_unit_1_p71[1]), .CLR(control_unit_1_p71[0]), .CLK(and_1_out),
    .OUTPUT(general_purpose_4_output));
  GENERAL_PURPOSE general_purpose_5 (
    .INPUT(alu_1_ex_4), .INC(control_unit_1_p81[8]), .LD(control_unit_1_p81[7]), .DEC(control_unit_1_p81[6]),
    .SHL(control_unit_1_p81[5]), .SHR(control_unit_1_p81[4]), .CIL(control_unit_1_p81[3]),
    .CIR(control_unit_1_p81[2]), .CML(control_unit_1_p81[1]), .CLR(control_unit_1_p81[0]), .CLK(and_1_out),
    .OUTPUT(general_purpose_5_output));
  Multiplexer #(.select(3), .width(16), .enable("false")) multiplexer_1 (
    .in0(special_purpose_1_output), .in1(general_purpose_1_output), .in2(general_purpose_2_output),
    .in3(general_purpose_3_output), .in4(general_purpose_4_output), .in5(general_purpose_5_output),
    .out(multiplexer_1_out), .sel(control_unit_1_p33));  // open: in6, in7
  assign controlled_buffer_1_out = control_unit_1_p43 ? {{8{1'b0}}, general_purpose_1_output} : 24'bz;  // Controlled_Buffer controlled_buffer_1
  assign controlled_buffer_1_out = control_unit_1_p53 ? {{8{1'b0}}, general_purpose_2_output} : 24'bz;  // Controlled_Buffer controlled_buffer_2
  assign controlled_buffer_1_out = control_unit_1_p63 ? {{8{1'b0}}, general_purpose_3_output} : 24'bz;  // Controlled_Buffer controlled_buffer_3
  assign controlled_buffer_1_out = control_unit_1_p73 ? {{8{1'b0}}, general_purpose_4_output} : 24'bz;  // Controlled_Buffer controlled_buffer_4
  assign controlled_buffer_1_out = control_unit_1_p83 ? {{8{1'b0}}, general_purpose_5_output} : 24'bz;  // Controlled_Buffer controlled_buffer_5
  SPECIAL_PURPOSE special_purpose_1 (
    .INPUT(controlled_buffer_1_out[15:0]), .INC(1'b0), .LD(control_unit_1_p89), .CLK(and_1_out),
    .OUTPUT(special_purpose_1_output));
  SPECIAL_PURPOSE special_purpose_2 (
    .INPUT(controlled_buffer_1_out[15:0]), .INC(control_unit_1_p85), .LD(control_unit_1_p86),
    .CLK(and_1_out), .OUTPUT(special_purpose_2_output));
  SPECIAL_PURPOSE special_purpose_3 (
    .INPUT(controlled_buffer_1_out[15:0]), .INC(1'b0), .LD(control_unit_1_p91), .CLK(and_1_out),
    .OUTPUT(special_purpose_3_output));
  INSTRUCTION_REGISTER instruction_register_1 (
    .INPUT(controlled_buffer_1_out), .LOAD(control_unit_1_p88), .CLK(and_1_out),
    .OUTPUT({instruction_register_1_output_2, instruction_register_1_output}));
  RAM #(.addrWidth(16), .dataWidth(24), .bus("separate")) ram_1 (
    .addr(multiplexer_1_out), .din(controlled_buffer_1_out), .data(ram_1_data), .str(control_unit_1_p31),
    .clk(and_1_out));  // open: sel, ld, clr
  assign controlled_buffer_1_out = control_unit_1_p90 ? {{8{1'b0}}, special_purpose_1_output} : 24'bz;  // Controlled_Buffer controlled_buffer_6
  assign controlled_buffer_1_out = control_unit_1_p84 ? {{8{1'b0}}, special_purpose_2_output} : 24'bz;  // Controlled_Buffer controlled_buffer_7
  assign controlled_buffer_1_out = control_unit_1_p87 ? {instruction_register_1_output_2, instruction_register_1_output} : 24'bz;  // Controlled_Buffer controlled_buffer_8
  assign controlled_buffer_1_out = control_unit_1_p32 ? ram_1_data : 24'bz;  // Controlled_Buffer controlled_buffer_9
  // Probe on control_unit_1_p7
  // Probe on control_unit_1_p6
  // Probe on general_purpose_1_output
  // Probe on general_purpose_2_output
  // Probe on general_purpose_3_output
  // Probe on general_purpose_4_output
  // Probe on general_purpose_5_output
  // Probe on controlled_buffer_1_out
  // Probe on special_purpose_1_output
  // Probe on special_purpose_2_output
  // Probe on special_purpose_3_output
  // Probe on {instruction_register_1_output_2, instruction_register_1_output}

  // Notes on the sheet:
  //   ZF
  //   CF
  //   AX
  //   BX
  //   CX
  //   DX
  //   EX
  //   AR
  //   PC
  //   DR
  //   IR
endmodule

module FLAG (
  input  INPUT,
  input  CLK,
  input  LOAD,
  input  CLR,
  input  CML,
  output out_6
);

  wire and_1_out, and_2_out, and_3_out, multiplexer_1_out, or_1_out, or_2_out, or_3_out;

  and and_1 (and_1_out, INPUT, LOAD);
  and and_2 (and_2_out, 1'b0, CLR);
  and and_3 (and_3_out, ~out_6, CML);  // AND_Gate
  or or_1 (or_1_out, and_1_out, and_2_out);
  or or_2 (or_2_out, and_3_out, or_1_out);
  or or_3 (or_3_out, LOAD, CLR, CML);
  Multiplexer #(.enable("false")) multiplexer_1 (.in0(out_6), .in1(or_2_out), .out(multiplexer_1_out), .sel(or_3_out));
  D_Flip_Flop d_ff_1 (.clk(CLK), .D(multiplexer_1_out), .Q(out_6));  // open: Qn, preset, en, reset
endmodule
